// Logisim project r32i_sc.circ as structural Verilog
module main (
  input  in_1
);

  wire clk, i_bus_sc_lb_be0_0, i_bus_sc_lb_be1_0, i_bus_sc_lb_be2_0, i_bus_sc_lb_be3_0, i_bus_sc_lb_we_o,
       i_bus_sc_mem_be0_o, i_bus_sc_mem_be1_o, i_bus_sc_mem_be2_o, i_bus_sc_mem_be3_o, i_bus_sc_mem_we_o,
       i_bus_sc_tty_we_o, i_rv32i_mem_be0_o, i_rv32i_mem_be1_o, i_rv32i_mem_be2_o, i_rv32i_mem_be3_o,
       i_rv32i_mem_wen_o;
  wire [31:0] d_ledbar_1_d_rd_o, d_ledbar_1_data_o, i_bus_sc_lb_data_o, i_bus_sc_mem_addr_o,
       i_bus_sc_mem_data_o, i_bus_sc_rdata_o, i_bus_sc_tty_data_o, i_rv32i_instr_addr, i_rv32i_mem_addr_o,
       i_rv32i_mem_dout_o, ram_1_dout, rom_1_data, shifter_1_out, shifter_2_out;

  ROM #(.addrWidth(12), .dataWidth(32)) rom_1 (.addr(shifter_1_out[11:0]), .data(rom_1_data));
  Shifter #(.shift("lr"), .width(32)) shifter_1 (.in(i_rv32i_instr_addr), .\dist (5'b00010), .out(shifter_1_out));
  Clock clock_1 (.out(clk));
  rv32i i_rv32i (
    .instr_addr(i_rv32i_instr_addr), .mem_wen_o(i_rv32i_mem_wen_o), .mem_be0_o(i_rv32i_mem_be0_o),
    .mem_be1_o(i_rv32i_mem_be1_o), .mem_be2_o(i_rv32i_mem_be2_o), .mem_be3_o(i_rv32i_mem_be3_o),
    .mem_addr_o(i_rv32i_mem_addr_o), .mem_dout_o(i_rv32i_mem_dout_o), .mem_din_i(i_bus_sc_rdata_o),
    .instr(rom_1_data), .rst_n(in_1), .clk(clk));
  sc_bus i_bus_sc (
    .lb_data_o(i_bus_sc_lb_data_o), .mem_data_o(i_bus_sc_mem_data_o), .tty_data_o(i_bus_sc_tty_data_o),
    .mem_addr_o(i_bus_sc_mem_addr_o), .mem_be0_o(i_bus_sc_mem_be0_o), .lb_be1_0(i_bus_sc_lb_be1_0),
    .mem_be1_o(i_bus_sc_mem_be1_o), .lb_be2_0(i_bus_sc_lb_be2_0), .mem_be2_o(i_bus_sc_mem_be2_o),
    .lb_be3_0(i_bus_sc_lb_be3_0), .mem_be3_o(i_bus_sc_mem_be3_o), .lb_be0_0(i_bus_sc_lb_be0_0),
    .rdata_o(i_bus_sc_rdata_o), .mem_we_o(i_bus_sc_mem_we_o), .tty_we_o(i_bus_sc_tty_we_o),
    .lb_we_o(i_bus_sc_lb_we_o), .addr_i(i_rv32i_mem_addr_o), .wdata_i(i_rv32i_mem_dout_o),
    .be1_i(i_rv32i_mem_be1_o), .be2_i(i_rv32i_mem_be2_o), .be3_i(i_rv32i_mem_be3_o),
    .be0_i(i_rv32i_mem_be0_o), .we_i(i_rv32i_mem_wen_o), .lb_data_i(d_ledbar_1_d_rd_o),
    .mem_data_i(ram_1_dout));
  RAM #(.addrWidth(12), .asyncread("true"), .byteenables("byteEnables"), .dataWidth(32)) ram_1 (
    .addr(shifter_2_out[11:0]), .we(i_bus_sc_mem_we_o), .oe(1'b1), .clk(clk), .din(i_bus_sc_mem_data_o),
    .dout(ram_1_dout), .be3(i_bus_sc_mem_be3_o), .be2(i_bus_sc_mem_be2_o), .be1(i_bus_sc_mem_be1_o),
    .be0(i_bus_sc_mem_be0_o));
  Shifter #(.shift("lr"), .width(32)) shifter_2 (.in(i_bus_sc_mem_addr_o), .\dist (5'b00010), .out(shifter_2_out));
  LedBar #(.matrixcols(32)) ledbar_1 (
    .led0(d_ledbar_1_data_o[31]), .led1(d_ledbar_1_data_o[30]), .led2(d_ledbar_1_data_o[29]),
    .led3(d_ledbar_1_data_o[28]), .led4(d_ledbar_1_data_o[27]), .led5(d_ledbar_1_data_o[26]),
    .led6(d_ledbar_1_data_o[25]), .led7(d_ledbar_1_data_o[24]), .led8(d_ledbar_1_data_o[23]),
    .led9(d_ledbar_1_data_o[22]), .led10(d_ledbar_1_data_o[21]), .led11(d_ledbar_1_data_o[20]),
    .led12(d_ledbar_1_data_o[19]), .led13(d_ledbar_1_data_o[18]), .led14(d_ledbar_1_data_o[17]),
    .led15(d_ledbar_1_data_o[16]), .led16(d_ledbar_1_data_o[15]), .led17(d_ledbar_1_data_o[14]),
    .led18(d_ledbar_1_data_o[13]), .led19(d_ledbar_1_data_o[12]), .led20(d_ledbar_1_data_o[11]),
    .led21(d_ledbar_1_data_o[10]), .led22(d_ledbar_1_data_o[9]), .led23(d_ledbar_1_data_o[8]),
    .led24(d_ledbar_1_data_o[7]), .led25(d_ledbar_1_data_o[6]), .led26(d_ledbar_1_data_o[5]),
    .led27(d_ledbar_1_data_o[4]), .led28(d_ledbar_1_data_o[3]), .led29(d_ledbar_1_data_o[2]),
    .led30(d_ledbar_1_data_o[1]), .led31(d_ledbar_1_data_o[0]));
  TTY #(.cols(100), .rows(16)) tty_1 (.data(i_bus_sc_tty_data_o[6:0]), .clk(clk), .we(i_bus_sc_tty_we_o), .clr(in_1));
  d_ledbar d_ledbar_1 (
    .data_o(d_ledbar_1_data_o), .d_rd_o(d_ledbar_1_d_rd_o), .d_i(i_bus_sc_lb_data_o),
    .be0_i(i_bus_sc_lb_be0_0), .be1_i(i_bus_sc_lb_be1_0), .be2_i(i_bus_sc_lb_be2_0),
    .be3_i(i_bus_sc_lb_be3_0), .wen_i(i_bus_sc_lb_we_o), .clk_i(clk), .rst_in(in_1));
  // Probe on ram_1_dout

  // Other names for the same wires on the sheet: rst_n = in_1

  // Notes on the sheet:
  //   contents of rom_1 (hex, n*v repeats v):
  //   13 3c000113 3c000ef ff0007b7 a7a023 8067 ff0007b7 7a503 8067 54783 78c63 ff000737 f72223 154783
  //   150513 fe079ae3 8067 fc010113 3312623 3412423 aaaab9b7 55555a37 3512223 3612023 1712e23 1812c23
  //   1912a23 1a12823 1b12623 2112e23 2812c23 2912a23 3212823 555a0a13 aaa98993 1ac00513 f95ff0ef 1e000513
  //   f8dff0ef 21400513 f85ff0ef 24800513 f7dff0ef 27c00513 f75ff0ef 800413 a0513 f51ff0ef 12*13 98513
  //   f19ff0ef 12*13 fff40413 ff47413 f80414e3 400913 100413 1f00493 fff48493 40513 ff4f493 ec1ff0ef
  //   141413 fe0496e3 1f00493 fff48493 40513 ff4f493 ea5ff0ef 145413 fe0496e3 fff90913 fc0912e3 513
  //   e8dff0ef 29800513 e9dff0ef 8000793 13 fff78793 ff7f793 fe079ae3 2a400513 e81ff0ef ee5ff06f 5f5f5f20
  //   20205f5f 5f202020 20205f20 20202020 5f5f2020 205f5f5f 2020205f 20202020 20202020 5f5f2020 205f5f5f a
  //   7c20207c 5f7c2020 207c5f5f 5f7c207c 20205f5f 5f207c20 7c20205f 5f5f7c5f 5f5f205f 5f5f205f 20207c5f
  //   7c20207c a 2020207c 207c2020 207c5f2d 207c207c 207c202e 20207c20 7c2d2020 205f7c20 20207c2d 5f5f7c5f
  //   20207c5f 7c20207c a 7c5f5f7c 5f7c5f5f 5f7c5f5f 5f7c5f7c 207c5f5f 5f5f7c20 7c5f5f7c 5f5f7c5f 5f5f7c5f
  //   20207c5f 5f5c2020 202f5f5f a 4c200a0a 6d207465 6f642065 6d6f7320 69687465 2e2e676e a2e 44200a0a
  //   a656e6f 0 6*a0a0a0a
endmodule

module rv32i_regbank (
  input  [3:0] rs1_16,
  input  is_upper,
  input  wen,
  input  [3:0] rd_16,
  input  [31:0] din,
  input  clk,
  input  rst_n,
  input  [3:0] rs2_16,
  output [31:0] rs1_d,
  output [31:0] rs2_d
);

  wire demultiplexer_1_out0, demultiplexer_1_out1, demultiplexer_1_out2, demultiplexer_1_out3,
       demultiplexer_1_out4, demultiplexer_1_out5, demultiplexer_1_out6, demultiplexer_1_out7,
       demultiplexer_2_out0, demultiplexer_2_out1, demultiplexer_2_out2, demultiplexer_2_out3,
       demultiplexer_2_out4, demultiplexer_2_out5, demultiplexer_2_out6, demultiplexer_2_out7, wen0, wen1;
  wire [31:0] multiplexer_1_out, multiplexer_2_out, multiplexer_3_out, multiplexer_4_out, multiplexer_5_out,
       x0_q, x1_q, x2_q, x3_q, x4_q, x5_q, x6_q, x7_q, x8_q, x9_q, x10_q, x11_q, x12_q, x13_q, x14_q, x15_q;

  and and_1 (wen1, wen, rd_16[3]);
  // Probe on din
  and and_2 (wen0, ~rd_16[3], wen);  // AND_Gate
  Demultiplexer #(.select(3)) demultiplexer_1 (
    .out0(demultiplexer_1_out0), .out1(demultiplexer_1_out1), .out2(demultiplexer_1_out2),
    .out3(demultiplexer_1_out3), .out4(demultiplexer_1_out4), .out5(demultiplexer_1_out5),
    .out6(demultiplexer_1_out6), .out7(demultiplexer_1_out7), .in(wen0), .sel(rd_16[2:0]));
  Register #(.width(32)) x0 (.D(din), .en(demultiplexer_1_out0), .Q(x0_q), .clk(clk), .clr(rst_n));
  Register #(.width(32)) x1 (.D(din), .en(demultiplexer_1_out1), .Q(x1_q), .clk(clk), .clr(rst_n));
  Register #(.width(32)) x2 (.D(din), .en(demultiplexer_1_out2), .Q(x2_q), .clk(clk), .clr(rst_n));
  Register #(.width(32)) x3 (.D(din), .en(demultiplexer_1_out3), .Q(x3_q), .clk(clk), .clr(rst_n));
  Register #(.width(32)) x4 (.D(din), .en(demultiplexer_1_out4), .Q(x4_q), .clk(clk), .clr(rst_n));
  Register #(.width(32)) x5 (.D(din), .en(demultiplexer_1_out5), .Q(x5_q), .clk(clk), .clr(rst_n));
  Register #(.width(32)) x6 (.D(din), .en(demultiplexer_1_out6), .Q(x6_q), .clk(clk), .clr(rst_n));
  Register #(.width(32)) x7 (.D(din), .en(demultiplexer_1_out7), .Q(x7_q), .clk(clk), .clr(rst_n));
  Multiplexer #(.width(32)) multiplexer_1 (.in0({32{1'b0}}), .in1(x0_q), .out(multiplexer_1_out), .sel(is_upper));
  Multiplexer #(.select(3), .width(32)) multiplexer_2 (
    .in0(multiplexer_1_out), .in1(x1_q), .in2(x2_q), .in3(x3_q), .in4(x4_q), .in5(x5_q), .in6(x6_q),
    .in7(x7_q), .out(multiplexer_2_out), .sel(rs1_16[2:0]));
  Multiplexer #(.select(3), .width(32)) multiplexer_3 (
    .in0(multiplexer_1_out), .in1(x1_q), .in2(x2_q), .in3(x3_q), .in4(x4_q), .in5(x5_q), .in6(x6_q),
    .in7(x7_q), .out(multiplexer_3_out), .sel(rs2_16[2:0]));
  Demultiplexer #(.select(3)) demultiplexer_2 (
    .out0(demultiplexer_2_out0), .out1(demultiplexer_2_out1), .out2(demultiplexer_2_out2),
    .out3(demultiplexer_2_out3), .out4(demultiplexer_2_out4), .out5(demultiplexer_2_out5),
    .out6(demultiplexer_2_out6), .out7(demultiplexer_2_out7), .in(wen1), .sel(rd_16[2:0]));
  Register #(.width(32)) x8 (.D(din), .en(demultiplexer_2_out0), .Q(x8_q), .clk(clk), .clr(rst_n));
  Register #(.width(32)) x9 (.D(din), .en(demultiplexer_2_out1), .Q(x9_q), .clk(clk), .clr(rst_n));
  Register #(.width(32)) x10 (.D(din), .en(demultiplexer_2_out2), .Q(x10_q), .clk(clk), .clr(rst_n));
  Register #(.width(32)) x11 (.D(din), .en(demultiplexer_2_out3), .Q(x11_q), .clk(clk), .clr(rst_n));
  Register #(.width(32)) x12 (.D(din), .en(demultiplexer_2_out4), .Q(x12_q), .clk(clk), .clr(rst_n));
  Register #(.width(32)) x13 (.D(din), .en(demultiplexer_2_out5), .Q(x13_q), .clk(clk), .clr(rst_n));
  Register #(.width(32)) x14 (.D(din), .en(demultiplexer_2_out6), .Q(x14_q), .clk(clk), .clr(rst_n));
  Register #(.width(32)) x15 (.D(din), .en(demultiplexer_2_out7), .Q(x15_q), .clk(clk), .clr(rst_n));
  Multiplexer #(.select(3), .width(32)) multiplexer_4 (
    .in0(x8_q), .in1(x9_q), .in2(x10_q), .in3(x11_q), .in4(x12_q), .in5(x13_q), .in6(x14_q), .in7(x15_q),
    .out(multiplexer_4_out), .sel(rs1_16[2:0]));
  Multiplexer #(.select(3), .width(32)) multiplexer_5 (
    .in0(x8_q), .in1(x9_q), .in2(x10_q), .in3(x11_q), .in4(x12_q), .in5(x13_q), .in6(x14_q), .in7(x15_q),
    .out(multiplexer_5_out), .sel(rs2_16[2:0]));
  Multiplexer #(.width(32)) multiplexer_6 (
    .in0(multiplexer_2_out), .in1(multiplexer_4_out), .out(rs1_d), .sel(rs1_16[3]));
  Multiplexer #(.width(32)) multiplexer_7 (
    .in0(multiplexer_3_out), .in1(multiplexer_5_out), .out(rs2_d), .sel(rs2_16[3]));

  // Other names for the same wires on the sheet: rd_8[2:0] = rd_16[2:0]
endmodule

module rv32i_regfile (
  input  [4:0] rs1,
  input  [31:0] din,
  input  [4:0] rd,
  input  wen,
  input  [4:0] rs2,
  input  clk,
  input  rst_n,
  output [31:0] rsa,
  output [31:0] rsb
);

  wire wen0, wen1;
  wire [31:0] i_reg0_rs1_d, i_reg0_rs2_d, i_reg1_rs1_d, i_reg1_rs2_d;

  and and_1 (wen1, wen, rd[4]);
  and and_2 (wen0, wen, ~rd[4]);  // AND_Gate
  rv32i_regbank i_reg0 (
    .rs1_d(i_reg0_rs1_d), .rs2_d(i_reg0_rs2_d), .clk(clk), .rst_n(rst_n), .rs2_16(rs2[3:0]), .wen(wen0),
    .rd_16(rd[3:0]), .is_upper(1'b0), .rs1_16(rs1[3:0]), .din(din));
  rv32i_regbank i_reg1 (
    .rs1_d(i_reg1_rs1_d), .rs2_d(i_reg1_rs2_d), .clk(clk), .rst_n(rst_n), .rs2_16(rs2[3:0]), .wen(wen1),
    .rd_16(rd[3:0]), .is_upper(1'b1), .rs1_16(rs1[3:0]), .din(din));
  Multiplexer #(.width(32)) multiplexer_1 (.in0(i_reg0_rs1_d), .in1(i_reg1_rs1_d), .out(rsa), .sel(rs1[4]));
  Multiplexer #(.width(32)) multiplexer_2 (.in0(i_reg0_rs2_d), .in1(i_reg1_rs2_d), .out(rsb), .sel(rs2[4]));
endmodule

module rv32i_alu (
  input  [31:0] rsa,
  input  [31:0] rsb_imm,
  input  op_add,
  input  op_ge,
  input  op_eq,
  input  op_ne,
  input  op_lt,
  input  op_geu,
  input  op_ltu,
  input  op_sub,
  input  op_and,
  input  op_or,
  input  op_xor,
  input  op_sll,
  input  op_srl,
  input  op_sra,
  input  op_rs2_imm,
  output [31:0] dout
);

  wire comparator_1_eq, comparator_1_gt, comparator_1_lt, comparator_2_eq, comparator_2_gt, comparator_2_lt,
       multiplexer_1_out, multiplexer_2_out, multiplexer_3_out, multiplexer_4_out, multiplexer_5_out,
       not_1_out, or_2_out, or_3_out, or_4_out;
  wire [31:0] adder_1_out, and_1_out, bit_extender_1_out, multiplexer_6_out, multiplexer_7_out,
       multiplexer_8_out, multiplexer_9_out, multiplexer_10_out, multiplexer_11_out, multiplexer_12_out,
       multiplexer_13_out, or_1_out, shifter_1_out, shifter_2_out, shifter_3_out, subtractor_1_out, xor_1_out;

  // Probe on op_add
  Adder #(.width(32)) adder_1 (.a(rsa), .b(rsb_imm), .out(adder_1_out));  // open: cin, cout
  Subtractor #(.width(32)) subtractor_1 (.a(rsa), .b(rsb_imm), .out(subtractor_1_out));  // open: bin, bout
  assign and_1_out = rsa & rsb_imm;  // AND_Gate and_1, 32 bits wide
  assign or_1_out = rsa | rsb_imm;  // OR_Gate or_1, 32 bits wide
  assign xor_1_out = rsa ^ rsb_imm;  // XOR_Gate xor_1, 32 bits wide
  Shifter #(.width(32)) shifter_1 (.in(rsa), .\dist (rsb_imm[4:0]), .out(shifter_1_out));
  Shifter #(.shift("lr"), .width(32)) shifter_2 (.in(rsa), .\dist (rsb_imm[4:0]), .out(shifter_2_out));
  Shifter #(.shift("ar"), .width(32)) shifter_3 (.in(rsa), .\dist (rsb_imm[4:0]), .out(shifter_3_out));
  Comparator #(.width(32)) comparator_1 (
    .a(rsa), .b(rsb_imm), .gt(comparator_1_gt), .eq(comparator_1_eq), .lt(comparator_1_lt));
  Comparator #(.mode("unsigned"), .width(32)) comparator_2 (
    .a(rsa), .b(rsb_imm), .gt(comparator_2_gt), .eq(comparator_2_eq), .lt(comparator_2_lt));
  or or_2 (or_2_out, comparator_1_gt, comparator_1_eq);
  Multiplexer multiplexer_1 (.in0(or_2_out), .in1(comparator_1_eq), .out(multiplexer_1_out), .sel(op_eq));
  or or_3 (or_3_out, comparator_2_gt, comparator_2_eq);
  Multiplexer multiplexer_2 (.in0(multiplexer_1_out), .in1(not_1_out), .out(multiplexer_2_out), .sel(op_ne));
  not not_1 (not_1_out, comparator_1_eq);
  Multiplexer multiplexer_3 (.in0(multiplexer_2_out), .in1(comparator_1_lt), .out(multiplexer_3_out), .sel(op_lt));
  Multiplexer multiplexer_4 (.in0(multiplexer_3_out), .in1(or_3_out), .out(multiplexer_4_out), .sel(op_geu));
  assign bit_extender_1_out = {{31{1'b0}}, multiplexer_5_out};  // Bit_Extender bit_extender_1
  Multiplexer multiplexer_5 (.in0(multiplexer_4_out), .in1(comparator_2_lt), .out(multiplexer_5_out), .sel(op_ltu));
  or or_4 (or_4_out, op_ge, op_eq, op_ne, op_lt, op_geu, op_ltu);
  Multiplexer #(.width(32)) multiplexer_6 (
    .in0(adder_1_out), .in1(subtractor_1_out), .out(multiplexer_6_out), .sel(op_sub));
  Multiplexer #(.width(32)) multiplexer_7 (
    .in0(multiplexer_6_out), .in1(and_1_out), .out(multiplexer_7_out), .sel(op_and));
  Multiplexer #(.width(32)) multiplexer_8 (
    .in0(multiplexer_7_out), .in1(or_1_out), .out(multiplexer_8_out), .sel(op_or));
  Multiplexer #(.width(32)) multiplexer_9 (
    .in0(multiplexer_8_out), .in1(xor_1_out), .out(multiplexer_9_out), .sel(op_xor));
  Multiplexer #(.width(32)) multiplexer_10 (
    .in0(multiplexer_9_out), .in1(shifter_1_out), .out(multiplexer_10_out), .sel(op_sll));
  Multiplexer #(.width(32)) multiplexer_11 (
    .in0(multiplexer_10_out), .in1(shifter_2_out), .out(multiplexer_11_out), .sel(op_srl));
  Multiplexer #(.width(32)) multiplexer_12 (
    .in0(multiplexer_11_out), .in1(shifter_3_out), .out(multiplexer_12_out), .sel(op_sra));
  Multiplexer #(.width(32)) multiplexer_13 (
    .in0(multiplexer_12_out), .in1(bit_extender_1_out), .out(multiplexer_13_out), .sel(or_4_out));
  Multiplexer #(.width(32)) multiplexer_14 (.in0(multiplexer_13_out), .in1(rsb_imm), .out(dout), .sel(op_rs2_imm));

  // Notes on the sheet:
  //   unsigned
endmodule

module rv32i_indec (
  input  [31:0] instr,
  output [4:0] rd,
  output [2:0] funct3,
  output [4:0] rs1,
  output [4:0] rs2,
  output [6:0] funct7,
  output [31:0] imm,
  output ar_r,
  output ar_i,
  output ld,
  output st,
  output br,
  output jal,
  output jalr,
  output lui,
  output auipc,
  output ebc
);

  wire or_1_out;
  wire [31:0] multiplexer_1_out, multiplexer_2_out, multiplexer_3_out, rv32i_imm_1_b_imm, rv32i_imm_1_i_imm,
       rv32i_imm_1_j_imm, rv32i_imm_1_s_imm, rv32i_imm_1_u_imm;

  rv32i_imm rv32i_imm_1 (
    .I_imm(rv32i_imm_1_i_imm), .S_imm(rv32i_imm_1_s_imm), .B_imm(rv32i_imm_1_b_imm),
    .U_imm(rv32i_imm_1_u_imm), .J_imm(rv32i_imm_1_j_imm), .instr(instr));
  Comparator #(.width(7)) comparator_1 (.a(instr[6:0]), .b(7'b0110011), .eq(ar_r));  // open: gt, lt
  Comparator #(.width(7)) comparator_2 (.a(instr[6:0]), .b(7'b0010011), .eq(ar_i));  // open: gt, lt
  Comparator #(.width(7)) comparator_3 (.a(instr[6:0]), .b(7'b0000011), .eq(ld));  // open: gt, lt
  Comparator #(.width(7)) comparator_4 (.a(instr[6:0]), .b(7'b0100011), .eq(st));  // open: gt, lt
  Comparator #(.width(7)) comparator_5 (.a(instr[6:0]), .b(7'b1100011), .eq(br));  // open: gt, lt
  Comparator #(.width(7)) comparator_6 (.a(instr[6:0]), .b(7'b1101111), .eq(jal));  // open: gt, lt
  Comparator #(.width(7)) comparator_7 (.a(instr[6:0]), .b(7'b1100111), .eq(jalr));  // open: gt, lt
  Comparator #(.width(7)) comparator_8 (.a(instr[6:0]), .b(7'b0110111), .eq(lui));  // open: gt, lt
  Comparator #(.width(7)) comparator_9 (.a(instr[6:0]), .b(7'b0010111), .eq(auipc));  // open: gt, lt
  Comparator #(.width(7)) comparator_10 (.a(instr[6:0]), .b(7'b1110011), .eq(ebc));  // open: gt, lt
  Multiplexer #(.width(32)) multiplexer_1 (
    .in0(rv32i_imm_1_i_imm), .in1(rv32i_imm_1_s_imm), .out(multiplexer_1_out), .sel(st));
  Multiplexer #(.width(32)) multiplexer_2 (
    .in0(multiplexer_1_out), .in1(rv32i_imm_1_b_imm), .out(multiplexer_2_out), .sel(br));
  Multiplexer #(.width(32)) multiplexer_3 (
    .in0(multiplexer_2_out), .in1(rv32i_imm_1_u_imm), .out(multiplexer_3_out), .sel(or_1_out));
  or or_1 (or_1_out, auipc, lui);
  Multiplexer #(.width(32)) multiplexer_4 (.in0(multiplexer_3_out), .in1(rv32i_imm_1_j_imm), .out(imm), .sel(jal));

  assign funct3 = instr[14:12];
  assign funct7 = instr[31:25];
  assign rd = instr[11:7];
  assign rs1 = instr[19:15];
  assign rs2 = instr[24:20];
endmodule

module rv32i_imm (
  input  [31:0] instr,
  output [31:0] I_imm,
  output [31:0] S_imm,
  output [31:0] B_imm,
  output [31:0] U_imm,
  output [31:0] J_imm
);

  // NoConnect on instr[6:0]
  assign {I_imm[31], B_imm[31:12]} = {{20{instr[31]}}, instr[31]};  // Bit_Extender bit_extender_1
  // NoConnect on I_imm[31]
  // NoConnect on {I_imm[31], B_imm[31:13]}
  // NoConnect on {I_imm[31], B_imm[31:24]}

  assign B_imm[11:0] = {instr[7], instr[30:25], instr[11:8], 1'b0};
  assign I_imm[30:0] = {B_imm[31:12], instr[30:20]};
  assign J_imm = {B_imm[23:12], instr[19:12], instr[20], instr[30:21], 1'b0};
  assign S_imm = {I_imm[31], B_imm[31:12], instr[30:25], instr[11:7]};
  assign U_imm = {B_imm[12], instr[30:12], {12{1'b0}}};

  // Notes on the sheet:
  //   I-imm
  //   S-imm
  //   B-imm
  //   U-imm
  //   J-imm
endmodule

module rv32i_aludec (
  input  [2:0] funct3,
  input  [6:0] funct7,
  input  ar_i,
  input  ar,
  input  br,
  input  lui_auipc,
  output op_add,
  output op_sub,
  output op_sll,
  output op_slt,
  output op_sltu,
  output op_xor,
  output op_srl,
  output op_sra,
  output op_or,
  output op_and,
  output op_beq,
  output op_bne,
  output op_blt,
  output op_bge,
  output op_bltu,
  output op_bgeu,
  output op_rs2_imm
);

  wire and_1_out, and_2_out, and_3_out, and_4_out, and_5_out, and_6_out, and_7_out, and_8_out, and_9_out,
       and_10_out, and_11_out, and_12_out, and_13_out, or_1_out, or_2_out;

  and and_1 (and_1_out, funct3[2], funct3[1], funct3[0]);
  or or_1 (or_1_out, ar_i, ar);
  and and_2 (and_2_out, funct3[2], funct3[1], ~funct3[0]);  // AND_Gate
  and and_3 (and_3_out, funct3[2], ~funct3[1], funct3[0]);  // AND_Gate
  and and_4 (and_4_out, funct7[5], and_3_out);
  and and_5 (and_5_out, and_3_out, ~funct7[5]);  // AND_Gate
  and and_6 (and_6_out, funct3[2], ~funct3[1], ~funct3[0]);  // AND_Gate
  and and_7 (and_7_out, ~funct3[2], funct3[1], funct3[0]);  // AND_Gate
  and and_8 (and_8_out, ~funct3[2], funct3[1], ~funct3[0]);  // AND_Gate
  and and_9 (and_9_out, ~funct3[2], ~funct3[1], funct3[0]);  // AND_Gate
  and and_10 (and_10_out, funct7[5], and_11_out);
  and and_11 (and_11_out, ~funct3[2], ~funct3[1], ~funct3[0]);  // AND_Gate
  and and_12 (and_12_out, and_11_out, ~funct7[5]);  // AND_Gate
  or or_2 (or_2_out, and_12_out, ar_i);
  and and_13 (and_13_out, ~ar_i, and_10_out);  // AND_Gate
  and and_14 (op_add, or_2_out, or_1_out);
  and and_15 (op_sub, or_1_out, and_13_out);
  and and_16 (op_sll, and_9_out, or_1_out);
  and and_17 (op_slt, and_8_out, or_1_out);
  and and_18 (op_sltu, and_7_out, or_1_out);
  and and_19 (op_xor, and_6_out, or_1_out);
  and and_20 (op_srl, and_5_out, or_1_out);
  and and_21 (op_sra, and_4_out, or_1_out);
  and and_22 (op_or, and_2_out, or_1_out);
  and and_23 (op_and, and_1_out, or_1_out);
  and and_24 (op_beq, and_11_out, br);
  and and_25 (op_bne, and_9_out, br);
  and and_26 (op_blt, and_6_out, br);
  and and_27 (op_bge, and_3_out, br);
  and and_28 (op_bltu, and_2_out, br);
  and and_29 (op_bgeu, and_1_out, br);

  assign op_rs2_imm = lui_auipc;
endmodule

module rv32i (
  input  [31:0] instr,
  input  [31:0] mem_din_i,
  input  clk,
  input  rst_n,
  output [31:0] instr_addr,
  output [31:0] mem_addr_o,
  output [31:0] mem_dout_o,
  output mem_wen_o,
  output mem_be0_o,
  output mem_be1_o,
  output mem_be2_o,
  output mem_be3_o
);

  wire and_1_out, i_decoder_op_add, i_decoder_op_and, i_decoder_op_beq, i_decoder_op_bge, i_decoder_op_bgeu,
       i_decoder_op_blt, i_decoder_op_bltu, i_decoder_op_bne, i_decoder_op_or, i_decoder_op_rs2_imm,
       i_decoder_op_sll, i_decoder_op_slt, i_decoder_op_sltu, i_decoder_op_sra, i_decoder_op_srl,
       i_decoder_op_sub, i_decoder_op_xor, i_indec_ar_i, i_indec_ar_r, i_indec_auipc, i_indec_br,
       i_indec_ebc, i_indec_jal, i_indec_jalr, i_indec_lui, i_indec_st, ld, not_1_out, not_2_out, not_3_out,
       or_1_out, or_2_out, or_3_out, or_4_out, or_5_out, or_6_out, or_7_out, or_8_out;
  wire [0:0] multiplexer_7_out;
  wire [2:0] i_indec_funct3;
  wire [4:0] i_indec_rd, i_indec_rs1, i_indec_rs2;
  wire [6:0] i_indec_funct7;
  wire [31:0] adder_1_out, i_alu_dout, i_indec_imm, i_regfile_rsa, i_regfile_rsb, multiplexer_1_out,
       multiplexer_2_out, multiplexer_3_out, multiplexer_4_out, multiplexer_5_out, multiplexer_6_out,
       rv32i_lsu_1_rdat_o;
  wire [31:1] multiplexer_7_out_2;

  // Probe on instr
  rv32i_indec i_indec (
    .rd(i_indec_rd), .funct3(i_indec_funct3), .rs1(i_indec_rs1), .rs2(i_indec_rs2), .funct7(i_indec_funct7),
    .imm(i_indec_imm), .ar_r(i_indec_ar_r), .ar_i(i_indec_ar_i), .ld(ld), .st(i_indec_st), .br(i_indec_br),
    .jal(i_indec_jal), .jalr(i_indec_jalr), .lui(i_indec_lui), .auipc(i_indec_auipc), .ebc(i_indec_ebc),
    .instr(instr));
  // Probe on i_indec_imm
  // NoConnect on i_indec_ebc
  Multiplexer #(.width(32)) multiplexer_1 (.in0(32'h4), .in1(i_indec_imm), .out(multiplexer_1_out), .sel(and_1_out));
  and and_1 (and_1_out, i_indec_br, multiplexer_7_out[0]);
  // Probe on i_indec_rs1
  // Probe on i_indec_rs2
  or or_1 (or_1_out, i_indec_jal, i_indec_jalr);
  // Probe on i_indec_rd
  or or_2 (or_2_out, i_indec_lui, i_indec_auipc);
  Adder #(.width(32)) adder_1 (.a(instr_addr), .b(multiplexer_1_out), .out(adder_1_out));  // open: cin, cout
  not not_1 (not_1_out, or_1_out);
  Multiplexer #(.width(32)) multiplexer_2 (
    .in0(adder_1_out), .in1({multiplexer_7_out_2, multiplexer_7_out[0]}), .out(multiplexer_2_out),
    .sel(not_1_out));
  rv32i_regfile i_regfile (
    .rsa(i_regfile_rsa), .rsb(i_regfile_rsb), .rs1(i_indec_rs1), .din(multiplexer_2_out), .rd(i_indec_rd),
    .wen(or_3_out), .rs2(i_indec_rs2), .clk(clk), .rst_n(rst_n));
  or or_3 (or_3_out, ld, or_1_out, or_2_out, i_indec_ar_i, i_indec_ar_r);
  // Probe on {multiplexer_7_out_2, multiplexer_7_out[0]}
  or or_4 (or_4_out, ld, or_2_out, i_indec_st, i_indec_ar_i, or_1_out);
  Multiplexer #(.width(32)) multiplexer_3 (
    .in0(i_indec_imm), .in1(i_regfile_rsb), .out(multiplexer_3_out), .sel(i_indec_st));
  Multiplexer #(.width(32)) multiplexer_4 (
    .in0(instr_addr), .in1(i_regfile_rsa), .out(multiplexer_4_out), .sel(not_2_out));
  Multiplexer #(.width(32)) multiplexer_5 (
    .in0(i_regfile_rsb), .in1(i_indec_imm), .out(multiplexer_5_out), .sel(or_4_out));
  not not_2 (not_2_out, or_5_out);
  or or_5 (or_5_out, i_indec_jal, or_2_out);
  // Probe on multiplexer_6_out
  Multiplexer #(.width(32)) multiplexer_6 (
    .in0(adder_1_out), .in1({multiplexer_7_out_2, 1'b0}), .out(multiplexer_6_out), .sel(or_1_out));
  or or_6 (or_6_out, or_1_out, i_decoder_op_add);
  or or_7 (or_7_out, i_decoder_op_slt, i_decoder_op_blt);
  rv32i_aludec i_decoder (
    .op_add(i_decoder_op_add), .op_sub(i_decoder_op_sub), .op_sll(i_decoder_op_sll),
    .op_slt(i_decoder_op_slt), .op_sltu(i_decoder_op_sltu), .op_xor(i_decoder_op_xor),
    .op_srl(i_decoder_op_srl), .op_sra(i_decoder_op_sra), .op_or(i_decoder_op_or), .op_and(i_decoder_op_and),
    .op_beq(i_decoder_op_beq), .op_bne(i_decoder_op_bne), .op_blt(i_decoder_op_blt),
    .op_bge(i_decoder_op_bge), .op_bltu(i_decoder_op_bltu), .op_bgeu(i_decoder_op_bgeu),
    .op_rs2_imm(i_decoder_op_rs2_imm), .funct7(i_indec_funct7), .br(i_indec_br), .lui_auipc(or_2_out),
    .funct3(i_indec_funct3), .ar_i(i_indec_ar_i), .ar(i_indec_ar_r));
  Register #(.width(32)) pc (.D(multiplexer_6_out), .Q(instr_addr), .clk(clk), .clr(rst_n));  // open: en
  or or_8 (or_8_out, i_decoder_op_sltu, i_decoder_op_bltu);
  Multiplexer #(.width(32)) multiplexer_7 (
    .in0(rv32i_lsu_1_rdat_o), .in1(i_alu_dout), .out({multiplexer_7_out_2, multiplexer_7_out[0]}),
    .sel(not_3_out));
  rv32i_alu i_alu (
    .dout(i_alu_dout), .op_or(i_decoder_op_or), .op_xor(i_decoder_op_xor), .op_sll(i_decoder_op_sll),
    .op_srl(i_decoder_op_srl), .op_sra(i_decoder_op_sra), .op_rs2_imm(i_decoder_op_rs2_imm),
    .rsb_imm(multiplexer_5_out), .rsa(multiplexer_4_out), .op_add(or_6_out), .op_ge(i_decoder_op_bge),
    .op_eq(i_decoder_op_beq), .op_ne(i_decoder_op_bne), .op_lt(or_7_out), .op_geu(i_decoder_op_bgeu),
    .op_ltu(or_8_out), .op_sub(i_decoder_op_sub), .op_and(i_decoder_op_and));
  not not_3 (not_3_out, ld);
  rv32i_lsu rv32i_lsu_1 (
    .wenmem_o(mem_wen_o), .wmem_o(mem_dout_o), .mem_addr_o(mem_addr_o), .rdat_o(rv32i_lsu_1_rdat_o),
    .be0_o(mem_be0_o), .be1_o(mem_be1_o), .be2_o(mem_be2_o), .be3_o(mem_be3_o), .func3_i(i_indec_funct3),
    .wdat_i(multiplexer_3_out), .mem_addr_i(i_alu_dout), .rmem_i(mem_din_i), .st_i(i_indec_st));

  // Other names for the same wires on the sheet: pc[31:0] = instr_addr

  // Notes on the sheet:
  //   take branch
endmodule

module rv32i_lsu (
  input  [31:0] wdat_i,
  input  [31:0] mem_addr_i,
  input  st_i,
  input  [31:0] rmem_i,
  input  [2:0] func3_i,
  output [31:0] wmem_o,
  output [31:0] mem_addr_o,
  output wenmem_o,
  output [31:0] rdat_o,
  output be0_o,
  output be1_o,
  output be2_o,
  output be3_o
);

  wire is_b, is_h, is_w;
  wire [3:0] multiplexer_10_out, shifter_11_out, shifter_12_out;
  wire [7:0] multiplexer_2_out;
  wire [15:0] multiplexer_6_out;
  wire [31:0] bit_extender_1_out, bit_extender_2_out, bit_extender_3_out, bit_extender_4_out,
       multiplexer_1_out, multiplexer_3_out, multiplexer_4_out, multiplexer_5_out, multiplexer_8_out,
       multiplexer_9_out, shifter_1_out, shifter_2_out, shifter_3_out, shifter_4_out, shifter_5_out,
       shifter_6_out, shifter_7_out, shifter_8_out, shifter_9_out, shifter_10_out;

  Shifter #(.width(32)) shifter_1 (.in(wdat_i), .\dist (5'b01000), .out(shifter_1_out));
  Shifter #(.width(32)) shifter_2 (.in(wdat_i), .\dist (5'b10000), .out(shifter_2_out));
  Shifter #(.width(32)) shifter_3 (.in(wdat_i), .\dist (5'b11000), .out(shifter_3_out));
  Shifter #(.shift("lr"), .width(32)) shifter_4 (.in(rmem_i), .\dist (5'b01000), .out(shifter_4_out));
  Shifter #(.shift("lr"), .width(32)) shifter_5 (.in(rmem_i), .\dist (5'b10000), .out(shifter_5_out));
  Shifter #(.shift("lr"), .width(32)) shifter_6 (.in(rmem_i), .\dist (5'b11000), .out(shifter_6_out));
  and and_1 (is_b, ~func3_i[0], ~func3_i[1]);  // AND_Gate
  and and_2 (is_h, func3_i[0], ~func3_i[1]);  // AND_Gate
  and and_3 (is_w, ~func3_i[0], func3_i[1]);  // AND_Gate
  Multiplexer #(.select(2), .width(32)) multiplexer_1 (
    .in0(wdat_i), .in1(shifter_1_out), .in2(shifter_2_out), .in3(shifter_3_out), .out(multiplexer_1_out),
    .sel(mem_addr_i[1:0]));
  Multiplexer #(.select(2), .width(8)) multiplexer_2 (
    .in0(rmem_i[7:0]), .in1(shifter_4_out[7:0]), .in2(shifter_5_out[7:0]), .in3(shifter_6_out[7:0]),
    .out(multiplexer_2_out), .sel(mem_addr_i[1:0]));
  Shifter #(.width(32)) shifter_7 (.in(wdat_i), .\dist (5'b01000), .out(shifter_7_out));
  Shifter #(.width(32)) shifter_8 (.in(wdat_i), .\dist (5'b10000), .out(shifter_8_out));
  Shifter #(.shift("lr"), .width(32)) shifter_9 (.in(rmem_i), .\dist (5'b01000), .out(shifter_9_out));
  Shifter #(.shift("lr"), .width(32)) shifter_10 (.in(rmem_i), .\dist (5'b10000), .out(shifter_10_out));
  assign bit_extender_1_out = {{24{multiplexer_2_out[7]}}, multiplexer_2_out};  // Bit_Extender bit_extender_1
  Multiplexer #(.width(32)) multiplexer_3 (
    .in0(bit_extender_1_out), .in1(bit_extender_2_out), .out(multiplexer_3_out), .sel(func3_i[2]));
  assign bit_extender_2_out = {{24{1'b0}}, multiplexer_2_out};  // Bit_Extender bit_extender_2
  Multiplexer #(.width(32)) multiplexer_4 (.in0(wdat_i), .in1(multiplexer_5_out), .out(multiplexer_4_out), .sel(is_h));
  Multiplexer #(.select(2), .width(32)) multiplexer_5 (
    .in0(wdat_i), .in1(shifter_7_out), .in2(shifter_8_out), .in3({32{1'b1}}), .out(multiplexer_5_out),
    .sel(mem_addr_i[1:0]));
  Multiplexer #(.select(2), .width(16)) multiplexer_6 (
    .in0(rmem_i[15:0]), .in1(shifter_9_out[15:0]), .in2(shifter_10_out[15:0]), .in3({16{1'b1}}),
    .out(multiplexer_6_out), .sel(mem_addr_i[1:0]));
  Multiplexer #(.width(32)) multiplexer_7 (.in0(multiplexer_4_out), .in1(multiplexer_1_out), .out(wmem_o), .sel(is_b));
  assign bit_extender_3_out = {{16{multiplexer_6_out[15]}}, multiplexer_6_out};  // Bit_Extender bit_extender_3
  Multiplexer #(.width(32)) multiplexer_8 (
    .in0(bit_extender_3_out), .in1(bit_extender_4_out), .out(multiplexer_8_out), .sel(func3_i[2]));
  assign bit_extender_4_out = {{16{1'b0}}, multiplexer_6_out};  // Bit_Extender bit_extender_4
  Shifter #(.width(4)) shifter_11 (.in(4'b0011), .\dist (mem_addr_i[1:0]), .out(shifter_11_out));
  Shifter #(.width(4)) shifter_12 (.in(4'b0001), .\dist (mem_addr_i[1:0]), .out(shifter_12_out));
  Multiplexer #(.width(32)) multiplexer_9 (.in0(rmem_i), .in1(multiplexer_8_out), .out(multiplexer_9_out), .sel(is_h));
  Multiplexer #(.width(4)) multiplexer_10 (.in0(4'b1111), .in1(shifter_11_out), .out(multiplexer_10_out), .sel(is_h));
  Multiplexer #(.width(32)) multiplexer_11 (.in0(multiplexer_9_out), .in1(multiplexer_3_out), .out(rdat_o), .sel(is_b));
  Multiplexer #(.width(4)) multiplexer_12 (
    .in0(multiplexer_10_out), .in1(shifter_12_out), .out({be3_o, be2_o, be1_o, be0_o}), .sel(is_b));

  assign mem_addr_o = mem_addr_i;
  assign wenmem_o = st_i;

  // Other names for the same wires on the sheet: is_unsigned = func3_i[2]; low_addr[1:0] = mem_addr_i[1:0]

  // Notes on the sheet:
  //   byte
  //   byte
  //   halfword
  //   WRITE
  //   READ
  //   halfword
endmodule

module sc_bus (
  input  be0_i,
  input  [31:0] wdata_i,
  input  be1_i,
  input  be2_i,
  input  be3_i,
  input  [31:0] addr_i,
  input  [31:0] lb_data_i,
  input  [31:0] mem_data_i,
  input  we_i,
  output lb_be0_0,
  output [31:0] lb_data_o,
  output mem_be0_o,
  output lb_be1_0,
  output mem_be1_o,
  output [31:0] mem_data_o,
  output lb_be2_0,
  output mem_be2_o,
  output [31:0] tty_data_o,
  output lb_be3_0,
  output mem_be3_o,
  output [31:0] mem_addr_o,
  output [31:0] rdata_o,
  output mem_we_o,
  output tty_we_o,
  output lb_we_o
);

  wire comparator_1_lt, comparator_2_eq, comparator_2_gt, comparator_3_lt, comparator_4_eq, comparator_4_gt,
       comparator_5_lt, comparator_6_eq, comparator_6_gt, is_lb_addr, is_mem_addr, is_tty_addr, or_1_out,
       or_2_out, or_3_out;
  wire [31:0] multiplexer_2_out;

  or or_1 (or_1_out, comparator_2_gt, comparator_2_eq);
  Comparator #(.mode("unsigned"), .width(32)) comparator_1 (
    .a(addr_i), .b(32'hff000000), .lt(comparator_1_lt));  // open: gt, eq
  Comparator #(.mode("unsigned"), .width(32)) comparator_2 (
    .a(addr_i), .b({32{1'b0}}), .gt(comparator_2_gt), .eq(comparator_2_eq));  // open: lt
  or or_2 (or_2_out, comparator_4_gt, comparator_4_eq);
  Comparator #(.mode("unsigned"), .width(32)) comparator_3 (
    .a(addr_i), .b(32'hff000004), .lt(comparator_3_lt));  // open: gt, eq
  Comparator #(.mode("unsigned"), .width(32)) comparator_4 (
    .a(addr_i), .b(32'hff000000), .gt(comparator_4_gt), .eq(comparator_4_eq));  // open: lt
  or or_3 (or_3_out, comparator_6_gt, comparator_6_eq);
  Comparator #(.mode("unsigned"), .width(32)) comparator_5 (
    .a(addr_i), .b(32'hff000008), .lt(comparator_5_lt));  // open: gt, eq
  Comparator #(.mode("unsigned"), .width(32)) comparator_6 (
    .a(addr_i), .b(32'hff000004), .gt(comparator_6_gt), .eq(comparator_6_eq));  // open: lt
  and and_1 (is_mem_addr, comparator_1_lt, or_1_out);
  and and_2 (is_lb_addr, comparator_3_lt, or_2_out);
  and and_3 (is_tty_addr, comparator_5_lt, or_3_out);
  Multiplexer #(.width(32)) multiplexer_1 (.in0(multiplexer_2_out), .in1(mem_data_i), .out(rdata_o), .sel(is_mem_addr));
  Multiplexer #(.width(32)) multiplexer_2 (
    .in0({32{1'b0}}), .in1(lb_data_i), .out(multiplexer_2_out), .sel(is_lb_addr));
  and and_4 (mem_we_o, we_i, is_mem_addr);
  and and_5 (tty_we_o, we_i, is_tty_addr);
  and and_6 (lb_we_o, we_i, is_lb_addr);

  assign lb_be0_0 = be0_i;
  assign lb_be1_0 = be1_i;
  assign lb_be2_0 = be2_i;
  assign lb_be3_0 = be3_i;
  assign lb_data_o = wdata_i;
  assign mem_addr_o = addr_i;
  assign mem_be0_o = be0_i;
  assign mem_be1_o = be1_i;
  assign mem_be2_o = be2_i;
  assign mem_be3_o = be3_i;
  assign mem_data_o = wdata_i;
  assign tty_data_o = wdata_i;
endmodule

module d_ledbar (
  input  [31:0] d_i,
  input  be0_i,
  input  be1_i,
  input  be2_i,
  input  be3_i,
  input  wen_i,
  input  clk_i,
  input  rst_in,
  output [31:0] data_o,
  output [31:0] d_rd_o
);

  wire and_1_out, and_2_out, and_3_out, and_4_out;

  Register register_1 (.D(d_i[7:0]), .en(and_1_out), .clk(clk_i), .Q(d_rd_o[7:0]), .clr(rst_in));
  and and_1 (and_1_out, be0_i, wen_i);
  Register register_2 (.D(d_i[15:8]), .en(and_2_out), .clk(clk_i), .Q(d_rd_o[15:8]), .clr(rst_in));
  and and_2 (and_2_out, be1_i, wen_i);
  Register register_3 (.D(d_i[23:16]), .en(and_3_out), .clk(clk_i), .Q(d_rd_o[23:16]), .clr(rst_in));
  and and_3 (and_3_out, be2_i, wen_i);
  Register register_4 (.D(d_i[31:24]), .en(and_4_out), .clk(clk_i), .Q(d_rd_o[31:24]), .clr(rst_in));
  and and_4 (and_4_out, be3_i, wen_i);

  assign data_o = d_rd_o;
endmodule
